# Fritzing sketch Schematic - Design Project Trashget (saved by Fritzing 0.9.3b)
breadboards: 1

parts:
  NodeMCU_ESP8266_V3 = NodeMCU V3.0
  Sensor_Ultrasonik_TPS_Anorganik = hc-sr04
  Sensor_Api = KY-026
  Sensor_Gas_MQ-2 = MQ-7 breakout
  VCC_+5v = 4 x AAA Battery Mount
  LED_Indikator_100% = smd LED [color="Red (633nm)" package="1206 [SMD]"]
  LED_Indikator_50% = smd LED [color="Yellow (585nm)" package="1206 [SMD]"]
  LED_Indikator_0% = smd LED [color="Green (555nm)" package="1206 [SMD]"]
  Sensor_Ultrasonik_TPS_Organik = hc-sr04
  R2 = Resistor [tolerance=±5% resistance=220 package="2010 [SMD]"]
  R3 = Resistor [tolerance=±5% resistance=220 package="2010 [SMD]"]
  R4 = Resistor [tolerance=±5% resistance=220 package="2010 [SMD]"]

nets:
  N1: NodeMCU_ESP8266_V3.D0, Sensor_Ultrasonik_TPS_Anorganik.Trig
  N2: NodeMCU_ESP8266_V3.D1, Sensor_Ultrasonik_TPS_Anorganik.Echo
  N3: NodeMCU_ESP8266_V3.D2, Sensor_Ultrasonik_TPS_Organik.Trig
  N4: NodeMCU_ESP8266_V3.D3, Sensor_Ultrasonik_TPS_Organik.Echo
  N5: NodeMCU_ESP8266_V3.D4, Sensor_Api.pin4
  GND: NodeMCU_ESP8266_V3.GND#6, NodeMCU_ESP8266_V3.GND#13, NodeMCU_ESP8266_V3.GND#16, NodeMCU_ESP8266_V3.GND#33, Sensor_Ultrasonik_TPS_Anorganik.GND, Sensor_Api.pin2, Sensor_Gas_MQ-2.GND, VCC_+5v.-, LED_Indikator_100%.cathode, LED_Indikator_50%.cathode, LED_Indikator_0%.cathode, Sensor_Ultrasonik_TPS_Organik.GND
  N6: NodeMCU_ESP8266_V3.D5, R4.Pin_1
  N7: NodeMCU_ESP8266_V3.D6, R2.Pin_1
  N8: NodeMCU_ESP8266_V3.D7, R3.Pin_1
  VCC: NodeMCU_ESP8266_V3.Vin, Sensor_Ultrasonik_TPS_Anorganik.VCC, Sensor_Api.pin3, Sensor_Gas_MQ-2.VCC, VCC_+5v.+, Sensor_Ultrasonik_TPS_Organik.VCC
  N9: NodeMCU_ESP8266_V3.A0, Sensor_Gas_MQ-2.DO
  N10: LED_Indikator_100%.anode, R4.Pin_0
  N11: LED_Indikator_50%.anode, R2.Pin_0
  N12: LED_Indikator_0%.anode, R3.Pin_0

notes:
  List Part
  1x NodeMCU ESP8266 V3
  1x Mini Breadboard
  1x Gas Sensor MQ-2
  1x Flame Sensor
  2x Ultrasonic Sensor HC-SR04
  3x LED (Red, Yellow, Green)
  3x 330ohm Resistor

custom parts:
  NodeMCU V3.0: ESP8266 based NodeMCU
  KY-026: ky-026 flame sensor module
  MQ-7 breakout: MQ-5 gas sensor
